// Logisim project Lab1-Boolean_Simplifier_Sayantan_Chaira_G_505.circ as structural Verilog: 1 circuit, main circuit main
module main (
  input  A,
  input  B,
  input  C,
  input  D,
  output F
);

  wire nA, nB, nC, nD, P1, P2, P3;

  not not_1 (nA, A);
  not not_2 (nB, B);
  not not_3 (nC, C);
  not not_4 (nD, D);
  and and_1 (P1, nB, nC);
  and and_2 (P2, nB, nD);
  and and_3 (P3, nA, nC, D);
  or or_1 (F, P1, P2, P3);
  LED led_1 (.in(F));

  // Notes on the sheet:
  //   Complements
  //   Lab 1  Simplified circuit: F(A,B,C,D) = Sum m(0,1,2,5,8,9,10)  =  B'C' + B'D' + A'C'D
  //   Verify: Project > Analyze Circuit > Table  (compare with the original 7 minterms)
  //   Prime implicants
  //   P1 = B'C'  (m0,1,8,9)
  //   P2 = B'D'  (m0,2,8,10)
  //   P3 = A'C'D  (m1,5)
  //   F (LED)
endmodule
