// Logisim project Lab2_NL_to_Logic_Vault_Sayantan_Chaira_G_505.circ as structural Verilog: 1 circuit, main circuit main
module main (
  input  M,
  input  C1,
  input  C2,
  input  T,
  output VAULT_OPEN,
  output ALARM
);

  wire ANYC, ANYKEY, nT;

  or or_1 (ANYC, C1, C2);
  not not_1 (nT, T);
  or or_2 (ANYKEY, M, C1, C2);
  and and_1 (VAULT_OPEN, M, ANYC, nT);
  and and_2 (ALARM, T, ANYKEY);
  LED led_1 (.in(VAULT_OPEN));
  LED led_2 (.in(ALARM));

  // Other names for the same wires on the sheet: OPEN = VAULT_OPEN

  // Notes on the sheet:
  //   M = manager's key
  //   C1 = clerk 1's key
  //   C2 = clerk 2's key
  //   T = time lock active (night)
  //   Lab 2  English -> logic: bank-vault door with time lock
  //   VAULT OPEN = M.(C1 + C2).T'      ALARM = T.(M + C1 + C2)
  //   Door unlock solenoid
  //   Alarm siren
endmodule
