// Logisim project Lab3_Traffic_Light_FSM_Sayantan_Chaira_G_505.circ as structural Verilog: 1 circuit, main circuit main
module main (
  input  PB,
  input  CLR
);

  wire CLK, GREEN, J0, JR, nQ0, nQ1, nWALK, Q0, Q1, R, WALK, YELLOW;

  Clock u_CLK (.out(CLK));
  and and_1 (JR, PB, nWALK);
  and and_2 (J0, nQ1, R);
  and and_3 (GREEN, nQ1, nQ0);
  and and_4 (YELLOW, nQ1, Q0);
  and and_5 (WALK, Q1, Q0);
  not not_1 (nWALK, WALK);
  J_K_Flip_Flop REQ (.J(JR), .clk(CLK), .K(WALK), .Q(R), .reset(CLR));  // open: Qn, preset, en
  J_K_Flip_Flop u_Q1 (.J(Q0), .clk(CLK), .K(nQ0), .Q(Q1), .Qn(nQ1), .reset(CLR));  // open: preset, en
  J_K_Flip_Flop u_Q0 (.J(J0), .clk(CLK), .K(Q1), .Q(Q0), .Qn(nQ0), .reset(CLR));  // open: preset, en
  LED led_1 (.in(Q1));
  LED led_2 (.in(YELLOW));
  LED led_3 (.in(GREEN));
  LED led_4 (.in(WALK));
  LED led_5 (.in(nWALK));
  LED led_6 (.in(R));

  // Notes on the sheet:
  //   PB = pedestrian push button
  //   (1 tick = one light period)
  //   Request latch
  //   Next-state logic
  //   Output logic
  //   Lab 3  Traffic light + pedestrian request (Moore FSM, JK)
  //   S0 GREEN=00  S1 YELLOW=01  S2 RED+WALK=11  S3 RED (clearance)=10   (Q1 Q0)
  //   State register
  //   Car lights
  //   RED
  //   YELLOW
  //   GREEN
  //   Pedestrian lights
  //   WALK
  //   DON'T WALK
  //   Request waiting
endmodule
