// Logisim project Lab4_Fault_Detection_FullAdder_Sayantan_Chaira_G_505.circ as structural Verilog: 1 circuit, main circuit main
module main (
  input  A,
  input  B,
  input  Cin,
  output S_faulty,
  output Cout_faulty,
  output S_fixed,
  output Cout_fixed
);

  wire dC, dS, ERR, fG, fH, fX, G, H, X;

  xor xor_1 (fX, A, B);
  and and_1 (fG, A, B);
  and and_2 (fH, B, Cin);
  xor xor_2 (X, A, B);
  and and_3 (G, A, B);
  and and_4 (H, X, Cin);
  xor xor_3 (S_faulty, fX, Cin);
  or or_1 (Cout_faulty, fG, fH);
  xor xor_4 (S_fixed, X, Cin);
  or or_2 (Cout_fixed, G, H);
  xor xor_5 (dS, S_faulty, S_fixed);
  xor xor_6 (dC, Cout_faulty, Cout_fixed);
  LED led_1 (.in(ERR));
  LED led_2 (.in(Cout_faulty));
  LED led_3 (.in(Cout_fixed));
  LED led_4 (.in(S_faulty));
  LED led_5 (.in(S_fixed));
  or or_3 (ERR, dS, dC);

  // Other names for the same wires on the sheet: C = Cout_fixed; fC = Cout_faulty; fS = S_faulty; S = S_fixed

  // Notes on the sheet:
  //   FAULTY adder (as built):  Cout = A.B + B.Cin   (term A.Cin missing)
  //   CORRECTED adder:  Cout = A.B + Cin.(A xor B)
  //   Lab 4  Fault detection: faulty full adder vs corrected full adder
  //   Fault detector
  //   MISMATCH (faulty differs from correct)
  //   Cout faulty
  //   Cout fixed
  //   Sum faulty
  //   Sum fixed
endmodule
