// Logisim project Lab5_24h_Digital_Clock_Sayantan_Chaira_G_505.circ as structural Verilog: 1 circuit, main circuit main
module main (
  input  CLR
);

  wire CLK, ha, hb, hH9, hJ1, hJ2, hJ3, hJT0, hJT1, hnQ3, hnT1, hnW, hQ0, hQ1, hQ2, hQ3, hT0, hT1, hW, hX,
       hZ, ma, mb, mCY, mE5, mJ1, mJ3, mJT1, mJT2, mnQ3, mnT2, mQ0, mQ1, mQ2, mQ3, mT0, mT1, mT2, mTC, sb,
       sCY, sE5, sJ1, sJ3, sJT1, sJT2, snQ3, snT2, sQ0, sQ1, sQ2, sQ3, sT0, sT1, sT2, sTC;

  Clock u_CLK (.out(CLK));
  and and_1 (ha, mCY, hQ0);
  and and_2 (hb, ha, hQ1);
  and and_3 (hJ1, ha, hnQ3);
  and and_4 (hJ3, hb, hQ2);
  and and_5 (hW, hT1, hQ1, hQ0);
  not not_1 (hnW, hW);
  and and_6 (hJ2, hb, hnW);
  and and_7 (hH9, hQ0, hQ3);
  or or_1 (hZ, hH9, hW);
  and and_8 (hX, mCY, hZ);
  and and_9 (hJT0, hX, hnT1);
  and and_10 (hJT1, hX, hT0);
  J_K_Flip_Flop HU0 (.J(mCY), .clk(CLK), .K(mCY), .Q(hQ0), .reset(CLR));  // open: Qn, preset, en
  J_K_Flip_Flop HU1 (.J(hJ1), .clk(CLK), .K(ha), .Q(hQ1), .reset(CLR));  // open: Qn, preset, en
  J_K_Flip_Flop HU2 (.J(hJ2), .clk(CLK), .K(hb), .Q(hQ2), .reset(CLR));  // open: Qn, preset, en
  J_K_Flip_Flop HU3 (.J(hJ3), .clk(CLK), .K(ha), .Q(hQ3), .Qn(hnQ3), .reset(CLR));  // open: preset, en
  Hex_Digit_Display hex_digit_display_1 (.value({2'b00, hT1, hT0}));  // open: dp
  Hex_Digit_Display hex_digit_display_2 (.value({hQ3, hQ2, hQ1, hQ0}));  // open: dp
  J_K_Flip_Flop u_HT0 (.J(hJT0), .clk(CLK), .K(hX), .Q(hT0), .reset(CLR));  // open: Qn, preset, en
  J_K_Flip_Flop u_HT1 (.J(hJT1), .clk(CLK), .K(hX), .Q(hT1), .Qn(hnT1), .reset(CLR));  // open: preset, en
  and and_11 (ma, sCY, mQ0);
  and and_12 (mb, ma, mQ1);
  and and_13 (mJ1, ma, mnQ3);
  and and_14 (mJ3, mb, mQ2);
  and and_15 (mTC, ma, mQ3);
  and and_16 (mE5, mTC, mT0);
  and and_17 (mJT1, mE5, mnT2);
  and and_18 (mJT2, mE5, mT1);
  and and_19 (mCY, mE5, mT2);
  J_K_Flip_Flop MU0 (.J(sCY), .clk(CLK), .K(sCY), .Q(mQ0), .reset(CLR));  // open: Qn, preset, en
  J_K_Flip_Flop MU1 (.J(mJ1), .clk(CLK), .K(ma), .Q(mQ1), .reset(CLR));  // open: Qn, preset, en
  J_K_Flip_Flop MU2 (.J(mb), .clk(CLK), .K(mb), .Q(mQ2), .reset(CLR));  // open: Qn, preset, en
  J_K_Flip_Flop MU3 (.J(mJ3), .clk(CLK), .K(ma), .Q(mQ3), .Qn(mnQ3), .reset(CLR));  // open: preset, en
  Hex_Digit_Display hex_digit_display_3 (.value({1'b0, mT2, mT1, mT0}));  // open: dp
  Hex_Digit_Display hex_digit_display_4 (.value({mQ3, mQ2, mQ1, mQ0}));  // open: dp
  J_K_Flip_Flop u_MT0 (.J(mTC), .clk(CLK), .K(mTC), .Q(mT0), .reset(CLR));  // open: Qn, preset, en
  J_K_Flip_Flop u_MT1 (.J(mJT1), .clk(CLK), .K(mE5), .Q(mT1), .reset(CLR));  // open: Qn, preset, en
  J_K_Flip_Flop u_MT2 (.J(mJT2), .clk(CLK), .K(mE5), .Q(mT2), .Qn(mnT2), .reset(CLR));  // open: preset, en
  and and_20 (sb, sQ0, sQ1);
  and and_21 (sJ1, sQ0, snQ3);
  and and_22 (sJ3, sb, sQ2);
  and and_23 (sTC, sQ0, sQ3);
  and and_24 (sE5, sTC, sT0);
  and and_25 (sJT1, sE5, snT2);
  and and_26 (sJT2, sE5, sT1);
  and and_27 (sCY, sE5, sT2);
  J_K_Flip_Flop SU0 (.J(1'b1), .clk(CLK), .K(1'b1), .Q(sQ0), .reset(CLR));  // open: Qn, preset, en
  J_K_Flip_Flop SU1 (.J(sJ1), .clk(CLK), .K(sQ0), .Q(sQ1), .reset(CLR));  // open: Qn, preset, en
  J_K_Flip_Flop SU2 (.J(sb), .clk(CLK), .K(sb), .Q(sQ2), .reset(CLR));  // open: Qn, preset, en
  J_K_Flip_Flop SU3 (.J(sJ3), .clk(CLK), .K(sQ0), .Q(sQ3), .Qn(snQ3), .reset(CLR));  // open: preset, en
  Hex_Digit_Display hex_digit_display_5 (.value({1'b0, sT2, sT1, sT0}));  // open: dp
  Hex_Digit_Display hex_digit_display_6 (.value({sQ3, sQ2, sQ1, sQ0}));  // open: dp
  J_K_Flip_Flop u_ST0 (.J(sTC), .clk(CLK), .K(sTC), .Q(sT0), .reset(CLR));  // open: Qn, preset, en
  J_K_Flip_Flop u_ST1 (.J(sJT1), .clk(CLK), .K(sE5), .Q(sT1), .reset(CLR));  // open: Qn, preset, en
  J_K_Flip_Flop u_ST2 (.J(sJT2), .clk(CLK), .K(sE5), .Q(sT2), .Qn(snT2), .reset(CLR));  // open: preset, en

  // Notes on the sheet:
  //   1 Hz in a real clock
  //   H tens
  //   HOURS (Mod-24)
  //   H units
  //   Lab 5  24-hour digital clock  HH:MM:SS  (synchronous, 20 JK flip-flops, BCD)
  //   M tens
  //   MINUTES (Mod-60)
  //   M units
  //   S tens
  //   SECONDS (Mod-60)
  //   S units
endmodule
