// Logisim project Lab6_1_JK_Register_Sayantan_Chaira_G_505.circ as structural Verilog: 1 circuit, main circuit main
module main (
  input  J,
  input  K,
  input  CLK_A,
  input  D0,
  input  D1,
  input  D2,
  input  D3,
  input  LOAD,
  input  CLK,
  input  CLR
);

  wire J0, J1, J2, J3, K0, K1, K2, K3, nD0, nD1, nD2, nD3, nQA, Q0, Q1, Q2, Q3, QA;

  J_K_Flip_Flop FF_A (.J(J), .clk(CLK_A), .K(K), .Q(QA), .Qn(nQA), .reset(CLR));  // open: preset, en
  not not_1 (nD0, D0);
  and and_1 (J0, D0, LOAD);
  and and_2 (K0, nD0, LOAD);
  not not_2 (nD1, D1);
  and and_3 (J1, D1, LOAD);
  and and_4 (K1, nD1, LOAD);
  not not_3 (nD2, D2);
  and and_5 (J2, D2, LOAD);
  and and_6 (K2, nD2, LOAD);
  not not_4 (nD3, D3);
  and and_7 (J3, D3, LOAD);
  and and_8 (K3, nD3, LOAD);
  LED led_1 (.in(QA));
  LED led_2 (.in(nQA));
  J_K_Flip_Flop BIT_0 (.J(J0), .clk(CLK), .K(K0), .Q(Q0), .reset(CLR));  // open: Qn, preset, en
  J_K_Flip_Flop BIT_1 (.J(J1), .clk(CLK), .K(K1), .Q(Q1), .reset(CLR));  // open: Qn, preset, en
  J_K_Flip_Flop BIT_2 (.J(J2), .clk(CLK), .K(K2), .Q(Q2), .reset(CLR));  // open: Qn, preset, en
  J_K_Flip_Flop BIT_3 (.J(J3), .clk(CLK), .K(K3), .Q(Q3), .reset(CLR));  // open: Qn, preset, en
  LED led_3 (.in(Q0));
  LED led_4 (.in(Q1));
  LED led_5 (.in(Q2));
  LED led_6 (.in(Q3));

  // Other names for the same wires on the sheet: CLKA = CLK_A; JA = J; KA = K

  // Notes on the sheet:
  //   Part A: JK flip-flop truth-table demo
  //   Part B: 4-bit register (each bit: J = D.LOAD,  K = D'.LOAD)
  //   Lab 6.1  JK Flip-Flop as a 1-bit memory cell / 4-bit register
  //   Q
  //   Q'
  //   Register outputs
  //   Q0
  //   Q1
  //   Q2
  //   Q3
endmodule
