// Logisim project Lab6_2_Mod60_Counter_Sayantan_Chaira_G_505.circ as structural Verilog: 1 circuit, main circuit main
module main (
  input  CLR
);

  wire CARRY, CLK, E5, J1, J2, J3, JT1, JT2, nQ3, nT2, Q0, Q1, Q2, Q3, T0, T1, T2, TC;

  Clock u_CLK (.out(CLK));
  and and_1 (J1, Q0, nQ3);
  and and_2 (J2, Q0, Q1);
  and and_3 (J3, Q0, Q1, Q2);
  and and_4 (TC, Q0, Q3);
  and and_5 (E5, TC, T0);
  and and_6 (JT1, E5, nT2);
  and and_7 (JT2, E5, T1);
  and and_8 (CARRY, E5, T2);
  J_K_Flip_Flop U0 (.J(1'b1), .clk(CLK), .K(1'b1), .Q(Q0), .reset(CLR));  // open: Qn, preset, en
  J_K_Flip_Flop U1 (.J(J1), .clk(CLK), .K(Q0), .Q(Q1), .reset(CLR));  // open: Qn, preset, en
  J_K_Flip_Flop U2 (.J(J2), .clk(CLK), .K(J2), .Q(Q2), .reset(CLR));  // open: Qn, preset, en
  J_K_Flip_Flop U3 (.J(J3), .clk(CLK), .K(Q0), .Q(Q3), .Qn(nQ3), .reset(CLR));  // open: preset, en
  J_K_Flip_Flop u_T0 (.J(TC), .clk(CLK), .K(TC), .Q(T0), .reset(CLR));  // open: Qn, preset, en
  J_K_Flip_Flop u_T1 (.J(JT1), .clk(CLK), .K(E5), .Q(T1), .reset(CLR));  // open: Qn, preset, en
  J_K_Flip_Flop u_T2 (.J(JT2), .clk(CLK), .K(E5), .Q(T2), .Qn(nT2), .reset(CLR));  // open: preset, en
  Hex_Digit_Display hex_digit_display_1 (.value({1'b0, T2, T1, T0}));  // open: dp
  LED led_1 (.in(CARRY));
  LED led_2 (.in(TC));
  Hex_Digit_Display hex_digit_display_2 (.value({Q3, Q2, Q1, Q0}));  // open: dp

  // Notes on the sheet:
  //   (1 Hz clock in a real clock)
  //   Next-state logic
  //   Lab 6.2  Synchronous Mod-60 counter (seconds counter of a digital clock) using JK FFs
  //   UNITS (Mod-10, BCD)
  //   TENS (Mod-6)
  //   TENS
  //   CARRY to minutes counter (=1 at 59)
  //   Units = 9 (enables tens)
  //   UNITS
endmodule
