// Logisim project Lab6_3_Shift_Registers_Sayantan_Chaira_G_505.circ as structural Verilog: 1 circuit, main circuit main
module main (
  input  CLK,
  input  CLR,
  input  DIN,
  input  P0,
  input  P1,
  input  P2,
  input  P3,
  input  LD
);

  wire A0, A1, A2, A3, B1, B2, B3, D1, D2, D3, nA0, nD1, nD2, nD3, nDIN, nS0, nS1, nS2, R0, R1, R2, R3, S0,
       S1, S2, S3, SH;

  not not_1 (nDIN, DIN);
  not not_2 (SH, LD);
  J_K_Flip_Flop u_S0 (.J(DIN), .clk(CLK), .K(nDIN), .Q(S0), .Qn(nS0), .reset(CLR));  // open: preset, en
  and and_1 (A0, LD, P0);
  and and_2 (A1, LD, P1);
  and and_3 (B1, SH, R0);
  and and_4 (A2, LD, P2);
  and and_5 (B2, SH, R1);
  and and_6 (A3, LD, P3);
  and and_7 (B3, SH, R2);
  J_K_Flip_Flop u_S1 (.J(S0), .clk(CLK), .K(nS0), .Q(S1), .Qn(nS1), .reset(CLR));  // open: preset, en
  not not_3 (nA0, A0);
  or or_1 (D1, A1, B1);
  not not_4 (nD1, D1);
  or or_2 (D2, A2, B2);
  not not_5 (nD2, D2);
  or or_3 (D3, A3, B3);
  not not_6 (nD3, D3);
  LED led_1 (.in(S0));
  J_K_Flip_Flop u_S2 (.J(S1), .clk(CLK), .K(nS1), .Q(S2), .Qn(nS2), .reset(CLR));  // open: preset, en
  LED led_2 (.in(S1));
  J_K_Flip_Flop u_R0 (.J(A0), .clk(CLK), .K(nA0), .Q(R0), .reset(CLR));  // open: Qn, preset, en
  J_K_Flip_Flop u_R1 (.J(D1), .clk(CLK), .K(nD1), .Q(R1), .reset(CLR));  // open: Qn, preset, en
  J_K_Flip_Flop u_R2 (.J(D2), .clk(CLK), .K(nD2), .Q(R2), .reset(CLR));  // open: Qn, preset, en
  J_K_Flip_Flop u_R3 (.J(D3), .clk(CLK), .K(nD3), .Q(R3), .reset(CLR));  // open: Qn, preset, en
  J_K_Flip_Flop u_S3 (.J(S2), .clk(CLK), .K(nS2), .Q(S3), .reset(CLR));  // open: Qn, preset, en
  LED led_3 (.in(S2));
  LED led_4 (.in(R0));
  LED led_5 (.in(R1));
  LED led_6 (.in(R2));
  LED led_7 (.in(R3));
  LED led_8 (.in(R3));
  LED led_9 (.in(S3));

  // Notes on the sheet:
  //   A) SIPO: serial in -> parallel out (UART receiver side)
  //   B) PISO: parallel in -> serial out (UART transmitter side).  LD=1 load, LD=0 shift
  //   Lab 6.3  4-bit Shift Registers with JK FFs (J = D, K = D')
  //   Parallel outputs:
  //   S0
  //   S1
  //   S2
  //   R0
  //   R1
  //   R2
  //   R3
  //   SERIAL OUT (TX line)
  //   S3
endmodule
