// Logisim project Lab7_Parking_Barrier_FSM_Sayantan_Chaira_G_505.circ as structural Verilog: 1 circuit, main circuit main
module main (
  input  A,
  input  S,
  input  F,
  input  CLK,
  input  CLR
);

  wire GREEN, J0, J1, K0, K1, nF, nQ0, nQ1, nS, Q0, Q1, WARN, X, Y;

  not not_1 (nS, S);
  not not_2 (nF, F);
  and and_1 (J1, Q0, S);
  and and_2 (K1, nQ0, nS);
  and and_3 (X, nQ1, A, nF);
  and and_4 (Y, Q1, S);
  or or_1 (J0, X, Y);
  and and_5 (K0, Q1, nS);
  J_K_Flip_Flop u_Q1 (.J(J1), .clk(CLK), .K(K1), .Q(Q1), .Qn(nQ1), .reset(CLR));  // open: preset, en
  J_K_Flip_Flop u_Q0 (.J(J0), .clk(CLK), .K(K0), .Q(Q0), .Qn(nQ0), .reset(CLR));  // open: preset, en
  and and_6 (GREEN, nQ1, Q0);
  and and_7 (WARN, Q1, nQ0);
  LED led_1 (.in(Q0));
  LED led_2 (.in(nQ0));
  LED led_3 (.in(GREEN));
  LED led_4 (.in(WARN));
  LED led_5 (.in(Q1));
  LED led_6 (.in(Q0));

  // Notes on the sheet:
  //   A = car at entry with valid ticket
  //   S = car under barrier (loop sensor)
  //   F = lot FULL
  //   Lab 7  Automatic Parking-Barrier Controller (Moore FSM, 2 JK FFs)
  //   S0 CLOSED=00   S1 OPEN=01   S2 CAR UNDER=11   S3 CLOSING=10   (Q1 Q0)
  //   Next-state (excitation) logic
  //   State register
  //   Output logic
  //   Outputs
  //   BARRIER UP (motor raise)
  //   RED light (stop)
  //   GREEN light (proceed)
  //   CLOSING warning buzzer
  //   state bit Q1
  //   state bit Q0
endmodule
