// Logisim project Lab8_1_ALU_4bit_Sayantan_Chaira_G_505.circ as structural Verilog: 1 circuit, main circuit main
module main (
  input  A0,
  input  A1,
  input  A2,
  input  A3,
  input  B0,
  input  B1,
  input  B2,
  input  B3,
  input  M
);

  wire C1, C2, C3, C4, G0, G1, G2, G3, H0, H1, H2, H3, nB0, nB1, nB2, nB3, nM, P0, P1, P2, P3, R0, R1, R2,
       R3, S0, S1, S2, S3, V, X0, X1, X2, X3, Y0, Y1, Y2, Y3;

  not not_1 (nM, M);
  not not_2 (nB0, B0);
  and and_1 (P0, nM, B0);
  and and_2 (R0, M, nB0);
  not not_3 (nB1, B1);
  and and_3 (P1, nM, B1);
  and and_4 (R1, M, nB1);
  not not_4 (nB2, B2);
  and and_5 (P2, nM, B2);
  and and_6 (R2, M, nB2);
  not not_5 (nB3, B3);
  and and_7 (P3, nM, B3);
  and and_8 (R3, M, nB3);
  or or_1 (Y0, P0, R0);
  or or_2 (Y1, P1, R1);
  or or_3 (Y2, P2, R2);
  or or_4 (Y3, P3, R3);
  xor xor_1 (X0, A0, Y0);
  and and_9 (G0, A0, Y0);
  xor xor_2 (X1, A1, Y1);
  and and_10 (G1, A1, Y1);
  xor xor_3 (X2, A2, Y2);
  and and_11 (G2, A2, Y2);
  xor xor_4 (X3, A3, Y3);
  and and_12 (G3, A3, Y3);
  xor xor_5 (S0, X0, M);
  and and_13 (H0, X0, M);
  xor xor_6 (S1, X1, C1);
  and and_14 (H1, X1, C1);
  xor xor_7 (S2, X2, C2);
  and and_15 (H2, X2, C2);
  xor xor_8 (S3, X3, C3);
  and and_16 (H3, X3, C3);
  or or_5 (C1, G0, H0);
  or or_6 (C2, G1, H1);
  or or_7 (C3, G2, H2);
  or or_8 (C4, G3, H3);
  xor xor_9 (V, C3, C4);
  LED led_1 (.in(S0));
  LED led_2 (.in(S1));
  LED led_3 (.in(S2));
  LED led_4 (.in(S3));
  LED led_5 (.in(C4));
  LED led_6 (.in(V));
  LED led_7 (.in(M));
  Hex_Digit_Display hex_digit_display_1 (.value({A3, A2, A1, A0}));  // open: dp
  Hex_Digit_Display hex_digit_display_2 (.value({B3, B2, B1, B0}));  // open: dp
  Hex_Digit_Display hex_digit_display_3 (.value({S3, S2, S1, S0}));  // open: dp

  // Notes on the sheet:
  //   M = mode select (0 add, 1 subtract)
  //   M is also the carry-in C0
  //   BIT 0
  //   BIT 1
  //   BIT 2
  //   BIT 3
  //   2:1 MUX per bit: Y = M'.B + M.B'
  //   Lab 8.1  4-bit Mini-ALU: adder/subtractor with mode-select MUX   (M=0: A+B,  M=1: A-B)
  //   Full adder per bit
  //   Overflow V = C3 xor C4
  //   S0
  //   S1
  //   S2
  //   S3
  //   COUT (carry out; in SUB = 1 means A >= B)
  //   OVERFLOW (signed)
  //   MODE: SUBTRACT
  //   A
  //   B
  //   RESULT
endmodule
