// Logisim project Lab8_2_Program_Counter_Sayantan_Chaira_G_505.circ as structural Verilog: 1 circuit, main circuit main
module main (
  input  EN,
  input  CLR
);

  wire CLK, nQ3, Q0, Q1, Q2, Q3, T1, T2, T3;

  Clock u_CLK (.out(CLK));
  and and_1 (T1, EN, Q0);
  and and_2 (T2, T1, Q1);
  and and_3 (T3, T2, Q2);
  not not_1 (nQ3, Q3);
  J_K_Flip_Flop PC0 (.J(EN), .clk(CLK), .K(EN), .Q(Q0), .reset(CLR));  // open: Qn, preset, en
  J_K_Flip_Flop PC1 (.J(T1), .clk(CLK), .K(T1), .Q(Q1), .reset(CLR));  // open: Qn, preset, en
  J_K_Flip_Flop PC2 (.J(T2), .clk(CLK), .K(T2), .Q(Q2), .reset(CLR));  // open: Qn, preset, en
  J_K_Flip_Flop PC3 (.J(T3), .clk(CLK), .K(T3), .Q(Q3), .reset(CLR));  // open: Qn, preset, en
  LED led_1 (.in(Q0));
  LED led_2 (.in(Q1));
  LED led_3 (.in(Q2));
  LED led_4 (.in(Q3));
  LED led_5 (.in(nQ3));
  LED led_6 (.in(Q3));
  Hex_Digit_Display hex_digit_display_1 (.value({Q3, Q2, Q1, Q0}));  // open: dp

  // Notes on the sheet:
  //   EN = 1: count (PC+1 / i++)
  //   CLR = 1: reset to 0 (i = 0)
  //   Toggle-enable chain
  //   Lab 8.2  4-bit Program Counter / loop counter (JK, synchronous, enable + reset)
  //   Q0
  //   Q1
  //   Q2
  //   Q3
  //   i < 8: loop body runs  (i<8 = Q3')
  //   i = 8: loop exits
  //   PC / i
endmodule
