// Logisim project Lab9_Comparator_MUX_Sayantan_Chaira_G_505.circ as structural Verilog: 1 circuit, main circuit main
module main (
  input  a1,
  input  a0,
  input  b1,
  input  b0
);

  wire c0, c1, D1, E1, G0, G1, GT, nb0, nb1, nGT, U0, U1, W0, W1;

  not not_1 (nb1, b1);
  not not_2 (nb0, b0);
  xor xor_1 (D1, a1, b1);
  not not_3 (E1, D1);
  not not_4 (nGT, GT);
  and and_1 (U1, GT, a1);
  and and_2 (W1, nGT, b1);
  and and_3 (U0, GT, a0);
  and and_4 (W0, nGT, b0);
  and and_5 (G1, a1, nb1);
  and and_6 (G0, E1, a0, nb0);
  or or_1 (c1, U1, W1);
  or or_2 (c0, U0, W0);
  or or_3 (GT, G1, G0);
  LED led_1 (.in(GT));
  LED led_2 (.in(nGT));
  LED led_3 (.in(c1));
  LED led_4 (.in(c0));
  Hex_Digit_Display hex_digit_display_1 (.value({2'b00, a1, a0}));  // open: dp
  Hex_Digit_Display hex_digit_display_2 (.value({2'b00, b1, b0}));  // open: dp
  Hex_Digit_Display hex_digit_display_3 (.value({2'b00, c1, c0}));  // open: dp

  // Notes on the sheet:
  //   Comparator: a > b
  //   2:1 MUX: c = GT ? a : b
  //   Lab 9  if (a > b) c = a; else c = b;   ->  2-bit comparator + 2:1 MUX
  //   GT = a1.b1' + (a1 xnor b1).a0.b0'
  //   a > b  (MUX selects a)
  //   a <= b (MUX selects b)
  //   c1
  //   c0
  //   a
  //   b
  //   c
endmodule
